# Fritzing sketch bbeeprog (saved by Fritzing 1.0.2b)
breadboards: 1

parts:
  IC2 = IC, DIP package, 20 pins [chip_label=SN74LV8153N]  # not connected
  IC1 = IC, DIP package, 20 pins [chip_label=SN74LV8153N]  # not connected
  IC3 = IC, DIP package, 28 pins [chip_label=AT28C256]
  IC4 = IC, DIP package, 20 pins [chip_label=SN74LV8153N]
  J1 = male pin header, 6 pins [form="♂ (male)"]

nets:
  N1: IC3.pin1, IC4.pin13
  N2: IC3.pin2, IC4.pin15
  N3: IC3.pin14, IC3.pin20, IC4.pin3, IC4.pin4, IC4.pin8, IC4.pin10, IC4.pin11, J1.pin6
  N4: IC3.pin21, IC4.pin17
  N5: IC3.pin22, IC3.pin28, IC4.pin1, IC4.pin2, IC4.pin6, IC4.pin7, IC4.pin20, J1.pin1, J1.pin2
  N6: IC3.pin23, IC4.pin16
  N7: IC3.pin24, IC4.pin18
  N8: IC3.pin25, IC4.pin19
  N9: IC3.pin26, IC4.pin14
  N10: IC3.pin27, IC4.pin12
  N11: IC4.pin5, J1.pin4

notes:
  5V
  VCC
  3V3
  TXD
  RXD
  GND
